// Logisim project Aula1.circ as structural Verilog: 4 circuits, main circuit main
module main (
  input  in_1,
  input  in_2,
  input  in_3,
  input  in_4,
  input  SAVE,
  input  reset,
  output out_7,
  output out_8,
  output out_9,
  output out_10
);

  D_Flip_Flop d_ff_1 (.clk(in_2), .D(in_1), .Q(out_7), .reset(reset));  // open: Qn, preset, en
  D_Flip_Flop d_ff_2 (.clk(in_2), .D(in_2), .Q(out_8), .reset(reset));  // open: Qn, preset, en
  D_Flip_Flop d_ff_3 (.clk(in_2), .D(in_2), .Q(out_9), .reset(reset));  // open: Qn, preset, en
  D_Flip_Flop d_ff_4 (.clk(in_2), .D(in_3), .Q(out_10), .reset(reset));  // open: Qn, preset, en

  assign in_4 = in_2;
  assign SAVE = in_2;
endmodule

module fp4bit (
  input  [3:0] INPUT,
  input  SAVE,
  input  Reset,
  output [3:0] OUT
);

  D_Flip_Flop d_ff_1 (.clk(SAVE), .D(INPUT[3]), .Q(OUT[3]), .reset(Reset));  // open: Qn, preset, en
  D_Flip_Flop d_ff_2 (.clk(SAVE), .D(INPUT[2]), .Q(OUT[2]), .reset(Reset));  // open: Qn, preset, en
  D_Flip_Flop d_ff_3 (.clk(SAVE), .D(INPUT[1]), .Q(OUT[1]), .reset(Reset));  // open: Qn, preset, en
  D_Flip_Flop d_ff_4 (.clk(SAVE), .D(INPUT[0]), .Q(OUT[0]), .reset(Reset));  // open: Qn, preset, en
endmodule

module fp8Bit (
  input  [3:0] in_1,
  input  in_2,
  input  in_3,
  input  in_4,
  input  in_5,
  input  in_6,
  input  in_7,
  input  in_8,
  input  in_9,
  input  in_10,
  output [3:0] out_11,
  output [3:0] out_12,
  output [3:0] out_13,
  output [3:0] out_14,
  output [3:0] out_15,
  output [3:0] out_16,
  output [3:0] out_17,
  output [3:0] out_18
);

  fp4bit fp4bit_1 (.SAVE(in_2), .Reset(in_3), .OUT(out_11), .INPUT(in_1));
  fp4bit fp4bit_2 (.SAVE(in_4), .Reset(in_3), .OUT(out_12), .INPUT(in_1));
  fp4bit fp4bit_3 (.SAVE(in_5), .Reset(in_3), .OUT(out_13), .INPUT(in_1));
  fp4bit fp4bit_4 (.SAVE(in_6), .Reset(in_3), .OUT(out_14), .INPUT(in_1));
  fp4bit fp4bit_5 (.SAVE(in_7), .Reset(in_3), .OUT(out_15), .INPUT(in_1));
  fp4bit fp4bit_6 (.SAVE(in_8), .Reset(in_3), .OUT(out_16), .INPUT(in_1));
  fp4bit fp4bit_7 (.SAVE(in_9), .Reset(in_3), .OUT(out_17), .INPUT(in_1));
  fp4bit fp4bit_8 (.SAVE(in_10), .Reset(in_3), .OUT(out_18), .INPUT(in_1));
endmodule

module FP8bitscompleta (
  input  [3:0] in_1,
  input  in_2,
  input  in_3,
  input  [2:0] WReg,
  output [3:0] out_5,
  output [2:0] RegA,
  output [3:0] out_7,
  output [2:0] RegB
);

  wire demultiplexer_1_out0, demultiplexer_1_out1, demultiplexer_1_out2, demultiplexer_1_out3,
       demultiplexer_1_out4, demultiplexer_1_out5, demultiplexer_1_out6, demultiplexer_1_out7;
  wire [3:0] fp4bit_1_out, fp4bit_2_out, fp4bit_3_out, fp4bit_4_out, fp4bit_5_out, fp4bit_6_out,
       fp4bit_7_out, fp4bit_8_out;

  Demultiplexer #(.select(3)) demultiplexer_1 (
    .out0(demultiplexer_1_out0), .out1(demultiplexer_1_out1), .out2(demultiplexer_1_out2),
    .out3(demultiplexer_1_out3), .out4(demultiplexer_1_out4), .out5(demultiplexer_1_out5),
    .out6(demultiplexer_1_out6), .out7(demultiplexer_1_out7), .in(in_3), .sel(WReg));  // open: en
  fp4bit fp4bit_1 (.SAVE(demultiplexer_1_out0), .Reset(in_2), .OUT(fp4bit_1_out), .INPUT(in_1));
  fp4bit fp4bit_2 (.SAVE(demultiplexer_1_out1), .Reset(in_2), .OUT(fp4bit_2_out), .INPUT(in_1));
  fp4bit fp4bit_3 (.SAVE(demultiplexer_1_out2), .Reset(in_2), .OUT(fp4bit_3_out), .INPUT(in_1));
  fp4bit fp4bit_4 (.SAVE(demultiplexer_1_out3), .Reset(in_2), .OUT(fp4bit_4_out), .INPUT(in_1));
  fp4bit fp4bit_5 (.SAVE(demultiplexer_1_out4), .Reset(in_2), .OUT(fp4bit_5_out), .INPUT(in_1));
  fp4bit fp4bit_6 (.SAVE(demultiplexer_1_out5), .Reset(in_2), .OUT(fp4bit_6_out), .INPUT(in_1));
  fp4bit fp4bit_7 (.SAVE(demultiplexer_1_out6), .Reset(in_2), .OUT(fp4bit_7_out), .INPUT(in_1));
  fp4bit fp4bit_8 (.SAVE(demultiplexer_1_out7), .Reset(in_2), .OUT(fp4bit_8_out), .INPUT(in_1));
  Multiplexer #(.select(3), .width(4)) multiplexer_1 (
    .in0(fp4bit_1_out), .in1(fp4bit_2_out), .in2(fp4bit_3_out), .in3(fp4bit_4_out), .in4(fp4bit_5_out),
    .in5(fp4bit_6_out), .in6(fp4bit_7_out), .in7(fp4bit_8_out), .out(out_5), .sel(RegA));  // open: en
  Multiplexer #(.select(3), .width(4)) multiplexer_2 (
    .in0(fp4bit_1_out), .in1(fp4bit_2_out), .in2(fp4bit_3_out), .in3(fp4bit_4_out), .in4(fp4bit_5_out),
    .in5(fp4bit_6_out), .in6(fp4bit_7_out), .in7(fp4bit_8_out), .out(out_7), .sel(RegB));  // open: en
endmodule
