// Logisim project ULA.circ as structural Verilog: 8 circuits, main circuit CelulaUla
module CelulaUla (
  input  b,
  input  a,
  input  in_3,
  input  [2:0] in_4,
  output out_5,
  output out_6
);

  wire or_1_out, somador_1_s, xor_1_out;

  Somador somador_1 (.CARRY_OUT(in_3), .B(b), .A(a), .S(somador_1_s), .CARRY_IN(out_6));
  and and_1 (b, a, b);
  or or_1 (or_1_out, a, b);
  xor xor_1 (xor_1_out, a, b);
  Multiplexer #(.select(3)) multiplexer_1 (
    .in0(b), .in1(or_1_out), .in2(somador_1_s), .in3(xor_1_out), .in4(b), .in5(b), .in6(b), .out(out_5),
    .sel(in_4));  // open: in7, en
endmodule

module mux_4_1 (
  input  A,
  input  B,
  input  C,
  input  D,
  input  SEL_0,
  input  SEL_1,
  output out_7
);

  wire mux2_1_1_out_4, mux2_1_2_out_4;

  Mux2_1 mux2_1_1 (.in_1(A), .in_2(B), .in_3(SEL_1), .out_4(mux2_1_1_out_4));
  Mux2_1 mux2_1_2 (.in_1(C), .in_2(D), .in_3(SEL_1), .out_4(mux2_1_2_out_4));
  Mux2_1 mux2_1_3 (.in_1(mux2_1_1_out_4), .in_2(mux2_1_2_out_4), .in_3(SEL_0), .out_4(out_7));
endmodule

module Ula_braulio (
  input  [3:0] in_1,
  input  [3:0] in_2,
  output [3:0] out_3
);

  wire celulaula_4_out_5;

  CelulaUla celulaula_1 ();  // open: out_6, b, a, in_4, out_5, in_3
  CelulaUla celulaula_2 ();  // open: out_6, b, a, in_4, out_5, in_3
  CelulaUla celulaula_3 ();  // open: out_6, b, a, in_4, out_5, in_3
  CelulaUla celulaula_4 (.out_5(celulaula_4_out_5));  // open: out_6, b, a, in_4, in_3
  // Pins of 2 and 4 bits meet at in_1
  // Pins of 2 and 4 bits meet at in_2
  // Pins of 2 and 4 bits meet at out_3
  // also tied to GND on the sheet: celulaula_4_out_5

  // Notes on the sheet:
  //   00 = and
  //   01 = or
  //   10 =soma
  //   11 = xor
endmodule

module ShiftleftArithmetic (
  input  [3:0] in_1,
  output [3:0] out_2
);


  assign out_2 = {in_1[2:0], 1'b0};
endmodule

module ShiftRightArithmetic (
  input  [3:0] in_1,
  output [3:0] out_2
);


  assign out_2 = {{2{in_1[3]}}, in_1[2:1]};
endmodule

module SLLdetect (
  input  [2:0] ULAOPCOde,
  output out_2
);

  and and_1 (out_2, ~ULAOPCOde[0], ~ULAOPCOde[1], ULAOPCOde[2]);  // AND_Gate
endmodule

module Mux2_1 (
  input  in_1,
  input  in_2,
  input  in_3,
  output out_4
);

  wire and_1_out, and_2_out;

  and and_1 (and_1_out, in_1, ~in_3);  // AND_Gate
  and and_2 (and_2_out, in_2, in_3);
  or or_1 (out_4, and_1_out, and_2_out);
endmodule

module Somador (
  input  B,
  input  A,
  input  CARRY_IN,
  output CARRY_OUT,
  output S
);

  wire and_1_out, and_2_out, and_3_out, xor_1_out;

  or or_1 (CARRY_OUT, and_2_out, and_1_out, and_3_out);
  and and_1 (and_1_out, B, A);
  and and_2 (and_2_out, CARRY_IN, B);
  and and_3 (and_3_out, A, CARRY_IN);
  xor xor_1 (xor_1_out, A, B);
  xor xor_2 (S, CARRY_IN, xor_1_out);
endmodule
